// Logisim project ex1.circ as structural Verilog: 1 circuit, main circuit generate_immediate
module generate_immediate (
  input  [31:0] INSTRUCTION,
  output [31:0] IMMEDIATE
);

  assign IMMEDIATE[31:12] = {{19{INSTRUCTION[31]}}, INSTRUCTION[31]};  // Bit_Extender bit_extender_1

  assign IMMEDIATE[11:0] = {INSTRUCTION[31:25], INSTRUCTION[11:7]};
endmodule
